# Fritzing sketch HomeCentral_Circuit1_004_NRF24L01 (saved by Fritzing 0.9.3b)
breadboards: 2

parts:
  M1 = DOIT Esp32 DevKit v1 (30 pins long, 11 pins width) [part_number=ESP32S-PIN30]
  U1 = LCD-16X2 [package=lcd-16x2]
  LCM1602_IIC2 = LCM1602 IIC [part_number="LCM1602 IIC" chip_label="LCM1602 IIC" package="DIP (Dual Inline) [THT]"]
  Part1 = Bluetooth HC-05 Macho  # not connected
  NRF24L3 = NRF24L01+ Breakout Board
  C2 = Electrolytic Capacitor [capacitance=10µF package="100 mil [THT, electrolytic]"]

nets:
  VCC: M1.3V3, LCM1602_IIC2.VCC, NRF24L3.VCC, C2.-
  GND: M1.GND, LCM1602_IIC2.GND, NRF24L3.GND, C2.+
  N1: M1.D21, M1.D22
  N2: M1.D26, NRF24L3.CE
  N3: M1.D27, NRF24L3.CS
  N4: M1.D14, NRF24L3.SCK
  N5: M1.D12, NRF24L3.MISO
  N6: M1.D13, NRF24L3.MOSI
  VSS: U1.VSS, LCM1602_IIC2.VSS
  VDD: U1.VDD, LCM1602_IIC2.VDD
  N7: U1.VO, LCM1602_IIC2.V0
  N8: U1.RS, LCM1602_IIC2.RS
  N9: U1.R_W, LCM1602_IIC2.RW
  N10: U1.E, LCM1602_IIC2.E
  N11: U1.DB0, LCM1602_IIC2.D0
  N12: U1.DB1, LCM1602_IIC2.D1
  N13: U1.DB2, LCM1602_IIC2.D2
  N14: U1.DB3, LCM1602_IIC2.D3
  N15: U1.DB4, LCM1602_IIC2.D4
  N16: U1.DB5, LCM1602_IIC2.D5
  N17: U1.DB6, LCM1602_IIC2.D6
  N18: U1.DB7, LCM1602_IIC2.D7
  N19: U1.A, LCM1602_IIC2.A
  N20: U1.K, LCM1602_IIC2.K
  N21: LCM1602_IIC2.SDA, LCM1602_IIC2.SCL

notes:
  The I2C Pins are not connected to the breadboard. The I2C module may be mounted on the LCD as a backpack.
  The NRF24L01 Pins are not connected to the breadboard. Use female-male connectors.
  10 micro Farad

custom parts:
  DOIT Esp32 DevKit v1 (30 pins long, 11 pins width): The DOIT Esp32 DevKit v1 is one of the development board created by DOIT to evaluate the ESP-WROOM-32 module. It is based on the ESP32 microcontroller that boasts Wifi, Bluetooth, Ethernet and Low Power support all in a single chip. (vanepp) made breadboard work, adjusted pin numbering and labels and reduced size of schematic and cleaned up pcb. This chip is 30pins long (2 x15) and 11 pins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
  LCM1602 IIC: I2C-Module to use a 1602 or 2004 LCD on with the wire.h libory Serial LCD Modul
