# Fritzing sketch HomeCentral_Circuit2_004_I2C (saved by Fritzing 0.9.4)

parts:
  U1 = ESP8266 NodeMCU LoLin base
  LCM1602_IIC1 = LCM1602 IIC [part_number="LCM1602 IIC" chip_label="LCM1602 IIC" package="DIP (Dual Inline) [THT]"]
  LCD1 = LCD screen
  U2 = 4-Channel 5v Relay Shield [package=relay-4ch5v10a]
  LED1 = LEDs [package=led10mm]
  Power_plug3 = Power plug
  LED2 = LEDs [package=led10mm]
  Power_plug4 = Power plug
  M1 = Humidity and Temperature Sensor DHT11
  Part1 = Bluetooth HC-05 Macho

nets:
  GND: U1.GND1-0, U1.GND3-0, U1.GND3-1, U1.GND3-2, U1.GND8-7, U1.GND8-9, U1.GND8-10, LCM1602_IIC1.GND, U2.GND, M1.GND, Part1.GND
  VCC: U1.3V1-0, U1.3V3-0, U1.3V3-2, LCM1602_IIC1.VCC, M1.Vcc
  N1: U1.D1-0, U1.D1-3, LCM1602_IIC1.SCL
  N2: U1.D2-0, U1.D2-3, LCM1602_IIC1.SDA
  N3: U1.D3-0, U2.IN1
  N4: U1.D4-0, U2.IN3
  N5: U1.D6-0, U1.D6-2, M1.Data
  N6: U1.RX-3, Part1.TXD
  N7: U1.TX-2, U1.TX-3, Part1.RXD
  VSS: LCM1602_IIC1.VSS, LCD1.VSS
  VDD: LCM1602_IIC1.VDD, LCD1.VDD
  N8: LCM1602_IIC1.V0, LCD1.V0
  N9: LCM1602_IIC1.RS, LCD1.RS
  N10: LCM1602_IIC1.RW, LCD1.R/W
  N11: LCM1602_IIC1.E, LCD1.E
  N12: LCM1602_IIC1.D0, LCD1.DB0
  N13: LCM1602_IIC1.D1, LCD1.DB1
  N14: LCM1602_IIC1.D2, LCD1.DB2
  N15: LCM1602_IIC1.D3, LCD1.DB3
  N16: LCM1602_IIC1.D4, LCD1.DB4
  N17: LCM1602_IIC1.D5, LCD1.DB5
  N18: LCM1602_IIC1.D6, LCD1.DB6
  N19: LCM1602_IIC1.D7, LCD1.DB7
  N20: LCM1602_IIC1.A, LCD1.LED+
  N21: LCM1602_IIC1.K, LCD1.LED-
  N22: U2.K1-In, LED1.C
  N23: U2.K1-Off, Power_plug3.VCC
  N24: U2.K3-In, LED2.C
  N25: U2.K3-Off, Power_plug4.VCC
  N26: LED1.A, Power_plug3.GND
  N27: LED2.A, Power_plug4.GND

notes:
  NodeMCU ESP8266 with a base board
  Use an 16x2 or a 20x4 LCD with a mounted I2C Backpack.
  Only the I2C connections need to be wired.
  Representative Electrical Device
  The polarity does not matter for an AC device but the relay should break the live wire.
  Connect to the NO (Normally Off) lead of the relay ouput.
  DHT11 Temperature and Humidity Sensor
  Relay may need 5V.
  Connect it to the Nano or an alternate 5V supply.
  HC05 needs 5V but NodeMCU ESP8266 only supplies 3V so connect it to the Nano.

custom parts:
  ESP8266 NodeMCU LoLin base: ESP8266 based NodeMCU Base
  LCM1602 IIC: I2C-Module to use a 1602 or 2004 LCD on with the wire.h libory Serial LCD Modul
  4-Channel 5v Relay Shield: 4 Channel 5v Relay Shield w. 2x SPD-06VDC-SD-C
  Humidity and Temperature Sensor DHT11: Digital relative humidity & temperature sensor DHT11
