# Fritzing sketch HomeCentral_Circuit2_004_SoilMoistureSensor (saved by Fritzing 0.9.4)
breadboards: 1

parts:
  Arduino_Nano = Arduino Nano (Rev3.0)
  HC-SR04_Sensor_1 = HC-SR04 Ultrasonic Distance Sensor
  S1 = Pushbutton [package="[THT]"]
  R3 = Resistor [tolerance=±5% resistance=10k package="2512 [SMD]"]
  Part5 = FC-28 Soil Hygrometer Module
  Part7 = FC-28 Soil Hygrometer Module - Probe
  R4 = Resistor [tolerance=±5% resistance=330 package="2512 [SMD]"]
  MQ-3_Sensor4 = MQ-3 Breakout Board  # not connected
  LED3 = RGB LED (com. cathode, rgb) [package="5 mm [THT]"]
  J1 = Piezo Speaker

nets:
  GND: Arduino_Nano.GND, HC-SR04_Sensor_1.GND, R3.Pin_1, R4.Pin_1, LED3.blue_anode, J1.pin1
  N1: Arduino_Nano.D2, S1.Pin_3, S1.Pin_4, R3.Pin_0
  N2: Arduino_Nano.D3, LED3.red_anode
  N3: Arduino_Nano.D6, LED3.green_anode
  N4: Arduino_Nano.D10, HC-SR04_Sensor_1.ECHO
  N5: Arduino_Nano.D11/MOSI, Arduino_Nano.D12/MISO, J1.pin2
  5V: Arduino_Nano.5V, HC-SR04_Sensor_1.VCC, S1.Pin_1, S1.Pin_2
  N6: Part5.POS, Part7.POS
  N7: Part5.NEG, Part7.NEG
  N8: R4.Pin_0, LED3.common_cathode

custom parts:
  FC-28 Soil Hygrometer Module: The FC-28 is a soil hygrometer module that uses the Texas Instruments LM393 comparator chip to provide an analog measurement of soil humidity. The digital output is high when soil moisture is over a certain threshold, as determined by adjusting the potentiometer.
  FC-28 Soil Hygrometer Module - Probe: The FC-28 is a soil hygrometer module that uses the Texas Instruments LM393 comparator chip to provide an analog measurement of soil humidity.
  MQ-3 Breakout Board: MQ-3 alcohol gas sensor breakout board. Input voltage is 5V. Sensor output is available in analog and digital.
