# Fritzing sketch HomeCentral_Circuit3_Complete (saved by Fritzing 0.9.4)
breadboards: 1

parts:
  Arduino_Nano = Arduino Nano (Rev3.0)
  S1 = Pushbutton [package="[THT]"]
  R3 = Resistor [tolerance=±5% resistance=10k package="2512 [SMD]"]
  LED2 = LED - 3mm [color="Green (555nm)" package="3 mm [THT]"]
  R4 = Resistor [tolerance=±5% resistance=330 package="2512 [SMD]"]
  KY-2 = Keyes Relay [package=THT]
  LED3 = LEDs [package=led10mm]
  Power_plug2 = Power plug
  LED4 = LEDs [package=led10mm]
  Power_plug3 = Power plug
  KY-3 = Keyes Relay [package=THT]
  PIR3 = PIR sensor
  Part2 = Bluetooth HC-05 Macho  # not connected

nets:
  GND: Arduino_Nano.GND, R3.Pin_1, R4.Pin_1, KY-2.ground, KY-3.ground, PIR3.GND
  N1: Arduino_Nano.D2, LED2.anode
  N2: Arduino_Nano.D3, S1.Pin_3, S1.Pin_4, R3.Pin_0
  N3: Arduino_Nano.D4, PIR3.SIG
  N4: Arduino_Nano.D5, KY-2.signal
  N5: Arduino_Nano.D6, KY-3.signal
  5V: Arduino_Nano.5V, S1.Pin_1, S1.Pin_2, KY-2.power, KY-3.power, PIR3.VDD
  N6: LED2.cathode, R4.Pin_0
  N7: LED3.A, Power_plug2.GND
  N8: LED4.A, Power_plug3.GND

custom parts:
  Keyes Relay: The Keyes 5V relay module is suitable for SCM development, home appliance control. It uses a 5V~12V TIL control signal which can control DC / AC signal.
