# Fritzing sketch Nano_UltrasonicDistanceSensor (saved by Fritzing 0.9.4)
breadboards: 1

parts:
  Arduino_Nano = Arduino Nano (Rev3.0)
  LED1 = LED - 5mm [color="Red (633nm)" package="5 mm [THT]"]
  HC-SR04_Sensor_1 = HC-SR04 Ultrasonic Distance Sensor
  LED2 = LED - 5mm [color="Red (633nm)" package="5 mm [THT]"]
  R1 = Resistor [tolerance=±5% resistance=680 package=THT]
  LED3 = LED - 5mm [color="Red (633nm)" package="5 mm [THT]"]
  R2 = Resistor [tolerance=±5% resistance=680 package=THT]
  R3 = Resistor [tolerance=±5% resistance=680 package=THT]

nets:
  GND: Arduino_Nano.GND, HC-SR04_Sensor_1.GND, R1.Pin_1, R2.Pin_1, R3.Pin_1
  N1: Arduino_Nano.D2, LED1.anode
  N2: Arduino_Nano.D3, LED2.anode
  N3: Arduino_Nano.D4, LED3.anode
  N4: Arduino_Nano.D9, Arduino_Nano.D10, HC-SR04_Sensor_1.ECHO
  5V: Arduino_Nano.5V, HC-SR04_Sensor_1.VCC
  N5: LED1.cathode, R1.Pin_0
  N6: LED2.cathode, R2.Pin_0
  N7: LED3.cathode, R3.Pin_0
