# Fritzing sketch P01_002_HomeCentral_Master_I2CLCD (saved by Fritzing 0.9.3b)
breadboards: 2

parts:
  M1 = DOIT Esp32 DevKit v1 (30 pins long, 11 pins width) [part_number=ESP32S-PIN30]
  U1 = LCD-16X2 [package=lcd-16x2]
  LCM1602_IIC2 = LCM1602 IIC [part_number="LCM1602 IIC" chip_label="LCM1602 IIC" package="DIP (Dual Inline) [THT]"]

nets:
  3V3: M1.3V3, LCM1602_IIC2.VCC
  GND: M1.GND, LCM1602_IIC2.GND
  N1: M1.D21, M1.D22, LCM1602_IIC2.SDA, LCM1602_IIC2.SCL
  VSS: U1.VSS, LCM1602_IIC2.VSS
  VDD: U1.VDD, LCM1602_IIC2.VDD
  N2: U1.VO, LCM1602_IIC2.V0
  N3: U1.RS, LCM1602_IIC2.RS
  N4: U1.R_W, LCM1602_IIC2.RW
  N5: U1.E, LCM1602_IIC2.E
  N6: U1.DB0, LCM1602_IIC2.D0
  N7: U1.DB1, LCM1602_IIC2.D1
  N8: U1.DB2, LCM1602_IIC2.D2
  N9: U1.DB3, LCM1602_IIC2.D3
  N10: U1.DB4, LCM1602_IIC2.D4
  N11: U1.DB5, LCM1602_IIC2.D5
  N12: U1.DB6, LCM1602_IIC2.D6
  N13: U1.DB7, LCM1602_IIC2.D7
  N14: U1.A, LCM1602_IIC2.A
  N15: U1.K, LCM1602_IIC2.K

notes:
  ESP32 runs on 3.3V and has no 5V output.
  The pin layout does not fit on one breadboard so use two connected boards.
  The I2C Pins are not connected to the breadboard. The I2C module may be mounted on the LCD as a backpack.

custom parts:
  DOIT Esp32 DevKit v1 (30 pins long, 11 pins width): The DOIT Esp32 DevKit v1 is one of the development board created by DOIT to evaluate the ESP-WROOM-32 module. It is based on the ESP32 microcontroller that boasts Wifi, Bluetooth, Ethernet and Low Power support all in a single chip. (vanepp) made breadboard work, adjusted pin numbering and labels and reduced size of schematic and cleaned up pcb. This chip is 30pins long (2 x15) and 11 pins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
  LCM1602 IIC: I2C-Module to use a 1602 or 2004 LCD on with the wire.h libory Serial LCD Modul
