# Fritzing sketch P04_002_HomeCentralAlexa_Slave1_Nano (saved by Fritzing 0.9.4)
breadboards: 1

parts:
  Arduino_Nano = Arduino Nano (Rev3.0)
  C1 = Electrolytic Capacitor [capacitance=10µF package="100 mil [THT, electrolytic]"]
  J1 = Piezo Speaker
  R1 = Resistor [tolerance=±5% resistance=100 package="2512 [SMD]"]
  MQ-3_Sensor3 = MQ-3 Breakout Board
  Part4 = FC-28 Soil Hygrometer Module
  Part6 = FC-28 Soil Hygrometer Module - Probe
  LED1 = LED - 5mm [color="Red (633nm)" package="5 mm [THT]"]
  R2 = Resistor [tolerance=±5% resistance=6.8k package=THT]  # not connected
  R3 = Resistor [tolerance=±5% resistance=6.8k package=THT]
  LED2 = smd LED [color="Green (555nm)" package="1206 [SMD]"]

nets:
  GND: Arduino_Nano.GND, C1.-, R1.Pin_0, MQ-3_Sensor3.GND, LED1.cathode, LED2.cathode
  N1: Arduino_Nano.D2, MQ-3_Sensor3.DOUT
  N2: Arduino_Nano.D5, J1.pin2
  N3: Arduino_Nano.D7, R3.Pin_0
  5V: Arduino_Nano.5V, C1.+, MQ-3_Sensor3.5V
  N4: Arduino_Nano.A1, MQ-3_Sensor3.AOUT
  N5: J1.pin1, R1.Pin_1
  N6: Part4.POS, Part6.POS
  N7: Part4.NEG, Part6.NEG
  N8: R3.Pin_1, LED2.anode

notes:
  5V Rails
  10 micro Farad
  Capacitor
  100 ohms
  Arduino
  Nano
  MQ-x
  Gas Sensor
  Soil Moisture
  Probe
  Soil Moisture Sensor
  Peizoelectric
  Buzzer
  LEDs for Soil Moisture - Red on low moisture, Green on OK

custom parts:
  MQ-3 Breakout Board: MQ-3 alcohol gas sensor breakout board. Input voltage is 5V. Sensor output is available in analog and digital.
  FC-28 Soil Hygrometer Module: The FC-28 is a soil hygrometer module that uses the Texas Instruments LM393 comparator chip to provide an analog measurement of soil humidity. The digital output is high when soil moisture is over a certain threshold, as determined by adjusting the potentiometer.
  FC-28 Soil Hygrometer Module - Probe: The FC-28 is a soil hygrometer module that uses the Texas Instruments LM393 comparator chip to provide an analog measurement of soil humidity.
