# Fritzing sketch arduino_nano_gas_sensor (saved by Fritzing 0.9.4)
breadboards: 1

parts:
  Arduino_Nano = Arduino Nano (Rev3.0)
  S1 = Pushbutton [package="[THT]"]
  R3 = Resistor [tolerance=±5% resistance=10k package="2512 [SMD]"]
  R4 = Resistor [tolerance=±5% resistance=330 package="2512 [SMD]"]
  MQ-3_Sensor4 = MQ-3 Breakout Board  # not connected
  LED3 = RGB LED (com. cathode, rgb) [package="5 mm [THT]"]

nets:
  N1: Arduino_Nano.GND, R3.Pin_1, R4.Pin_1, LED3.blue_anode
  N2: Arduino_Nano.D2, S1.Pin_3, S1.Pin_4, R3.Pin_0
  N3: Arduino_Nano.D3, LED3.red_anode
  N4: Arduino_Nano.D6, LED3.green_anode
  N5: Arduino_Nano.5V, S1.Pin_1, S1.Pin_2
  N6: R4.Pin_0, LED3.common_cathode

custom parts:
  MQ-3 Breakout Board: MQ-3 alcohol gas sensor breakout board. Input voltage is 5V. Sensor output is available in analog and digital.
