# Fritzing sketch arduino_nano_onboard_led (saved by Fritzing 0.9.4)
breadboards: 1

parts:
  Arduino_Nano = Arduino Nano (Rev3.0)
  S1 = Pushbutton [package="[THT]"]
  R3 = Resistor [tolerance=±5% resistance=10k package="2512 [SMD]"]
  R4 = Resistor [tolerance=±5% resistance=330 package="2512 [SMD]"]
  LED3 = RGB LED (com. cathode, rgb) [package="5 mm [THT]"]

nets:
  N1: Arduino_Nano.GND, R3.Pin_1, R4.Pin_1, LED3.blue_anode
  N2: Arduino_Nano.D2, S1.Pin_3, S1.Pin_4, R3.Pin_0
  N3: Arduino_Nano.D3, LED3.red_anode
  N4: Arduino_Nano.D6, LED3.green_anode
  5V: Arduino_Nano.5V, Arduino_Nano.3V3, S1.Pin_1, S1.Pin_2
  N5: R4.Pin_0, LED3.common_cathode

notes:
  3.3V Rails
  5V Rails
