# Fritzing sketch arduino_nano_relay (saved by Fritzing 0.9.4)
breadboards: 1

parts:
  Arduino_Nano = Arduino Nano (Rev3.0)
  S1 = Pushbutton [package="[THT]"]
  R3 = Resistor [tolerance=±5% resistance=10k package="2512 [SMD]"]
  LED2 = LED - 3mm [color="Green (555nm)" package="3 mm [THT]"]
  R4 = Resistor [tolerance=±5% resistance=330 package="2512 [SMD]"]
  KY-2 = Keyes Relay [package=THT]
  LED3 = LEDs [package=led10mm]
  Power_plug2 = Power plug
  LED4 = LEDs [package=led10mm]
  Power_plug3 = Power plug
  KY-3 = Keyes Relay [package=THT]

nets:
  N1: Arduino_Nano.GND, R3.Pin_1, R4.Pin_1, KY-2.ground, KY-3.ground
  N2: Arduino_Nano.D2, LED2.anode
  N3: Arduino_Nano.D3, S1.Pin_3, S1.Pin_4, R3.Pin_0
  N4: Arduino_Nano.D5, KY-2.signal
  N5: Arduino_Nano.D6, KY-3.signal
  N6: Arduino_Nano.5V, S1.Pin_1, S1.Pin_2, KY-2.power, KY-3.power
  N7: LED2.cathode, R4.Pin_0
  N8: LED3.A, Power_plug2.GND
  N9: LED4.A, Power_plug3.GND

custom parts:
  Keyes Relay: The Keyes 5V relay module is suitable for SCM development, home appliance control. It uses a 5V~12V TIL control signal which can control DC / AC signal.
