# Fritzing sketch nodemcu_i2c_lcd (saved by Fritzing 0.9.4)
breadboards: 1

parts:
  U1 = ESP8266 NodeMCU LoLin base
  LED1 = LED - 3mm [color="Green (555nm)" package="3 mm [THT]"]
  S1 = Pushbutton [package="[THT]"]
  R1 = Resistor [tolerance=±5% resistance=330 package="2512 [SMD]"]
  R2 = Resistor [tolerance=±5% resistance=330 package="2512 [SMD]"]
  LCM1602_IIC3 = LCM1602 IIC [part_number="LCM1602 IIC" chip_label="LCM1602 IIC" package="DIP (Dual Inline) [THT]"]
  LCD3 = LCD screen

nets:
  N1: U1.GND1-0, U1.GND2-0, R1.Pin_1, R2.Pin_1, LCM1602_IIC3.GND
  N2: U1.3V1-1, U1.3V3-2, S1.Pin_1, S1.Pin_2, LCM1602_IIC3.VCC
  N3: U1.D1-0, U1.D1-3, LCM1602_IIC3.SCL
  N4: U1.D2-0, U1.D2-3, LCM1602_IIC3.SDA
  N5: U1.D3-0, LED1.anode
  N6: U1.D5-0, U1.D5-2, U1.D5-3, S1.Pin_3, S1.Pin_4, R2.Pin_0
  N7: LED1.cathode, R1.Pin_0
  VSS: LCM1602_IIC3.VSS, LCD3.VSS
  VDD: LCM1602_IIC3.VDD, LCD3.VDD
  N8: LCM1602_IIC3.V0, LCD3.V0
  N9: LCM1602_IIC3.RS, LCD3.RS
  N10: LCM1602_IIC3.RW, LCD3.R/W
  N11: LCM1602_IIC3.E, LCD3.E
  N12: LCM1602_IIC3.D0, LCD3.DB0
  N13: LCM1602_IIC3.D1, LCD3.DB1
  N14: LCM1602_IIC3.D2, LCD3.DB2
  N15: LCM1602_IIC3.D3, LCD3.DB3
  N16: LCM1602_IIC3.D4, LCD3.DB4
  N17: LCM1602_IIC3.D5, LCD3.DB5
  N18: LCM1602_IIC3.D6, LCD3.DB6
  N19: LCM1602_IIC3.D7, LCD3.DB7
  N20: LCM1602_IIC3.A, LCD3.LED+
  N21: LCM1602_IIC3.K, LCD3.LED-

notes:
  NodeMCU ESP8266
  with a base board

custom parts:
  ESP8266 NodeMCU LoLin base: ESP8266 based NodeMCU Base
  LCM1602 IIC: I2C-Module to use a 1602 or 2004 LCD on with the wire.h libory Serial LCD Modul
