# Fritzing sketch nodemcu_onboard_led (saved by Fritzing 0.9.4)
breadboards: 1

parts:
  U1 = ESP8266 NodeMCU LoLin base
  LED1 = LED - 3mm [color="Green (555nm)" package="3 mm [THT]"]
  S1 = Pushbutton [package="[THT]"]
  R1 = Resistor [tolerance=±5% resistance=330 package="2512 [SMD]"]
  R2 = Resistor [tolerance=±5% resistance=330 package="2512 [SMD]"]

nets:
  N1: U1.GND1-0, U1.GND2-1, R1.Pin_1, R2.Pin_1
  N2: U1.3V1-1, U1.3V3-2, S1.Pin_1, S1.Pin_2
  N3: U1.D3-0, LED1.anode
  N4: U1.D5-0, U1.D5-2, U1.D5-3, S1.Pin_3, S1.Pin_4, R2.Pin_0
  N5: LED1.cathode, R1.Pin_0

notes:
  NodeMCU ESP8266
  with a base board

custom parts:
  ESP8266 NodeMCU LoLin base: ESP8266 based NodeMCU Base
